# Fritzing sketch IR (saved by Fritzing 0.9.3b)
breadboards: 1

parts:
  パーツ1 = Arduino Uno (Rev3)
  LED1 = LED - 5mm [color="Infrared (940nm)" package="5 mm [THT]"]
  LED2 = LED - 5mm [color="Infrared (940nm)" package="5 mm [THT]"]
  LED3 = LED - 5mm [color="Infrared (940nm)" package="5 mm [THT]"]
  R1 = Resistor [tolerance=±5% resistance=100 package=THT]
  R2 = Resistor [tolerance=±5% resistance=100 package=THT]
  R3 = Resistor [tolerance=±5% resistance=100 package=THT]
  2SC1815 = NPN-Transistor [package="TO92 [THT]"]
  R4 = Resistor [tolerance=±5% resistance=4.7k package=THT]
  PL-IRM2121-A538 = Infra red receiver

nets (from the schematic view):
  N1: パーツ1.D11_PWM/MOSI, PL-IRM2121-A538.Data
  GND: パーツ1.GND, LED1.anode, 2SC1815.E, PL-IRM2121-A538.GND
  N2: パーツ1.D3_PWM, R4.Pin_0
  5V: パーツ1.5V, PL-IRM2121-A538.VCC
  N3: LED1.cathode, R1.Pin_0
  N4: LED2.cathode, R2.Pin_0
  N5: LED3.cathode, R3.Pin_1
  N6: R1.Pin_1, R2.Pin_1, R3.Pin_0, 2SC1815.B
  N7: 2SC1815.C, R4.Pin_1
